# Fritzing sketch NFC_reader_test1 (saved by Fritzing 0.9.10b)
breadboards: 1

parts:
  A1 = Esp32-c3 super mini
  D1 = Schottky Diode [part_number=1N5817 package="300 mil [THT]"]
  V2 = DC Power [voltage=4.2V]
  U1 = RFID RC522 SIP - 8 pins [chip_label="RFID RC522" package="SIP (Single Inline) [THT]"]

nets:
  N1: A1.Pin_1, U1.MISO
  N2: A1.Pin_2, U1.MOSI
  N3: A1.Pin_3, U1.NSS
  N4: A1.Pin_4, U1.RST
  N5: A1.Pin_13, U1.SCK
  3.3V: A1.Pin_14, D1.cathode, U1.VCC
  GND: A1.Pin_15, V2.V-, U1.GND
  N6: D1.anode, V2.V+

notes:
  zf240510.1452
  zf240510.1521

custom parts:
  Esp32-c3 super mini: ESP32-C3 Development Board ESP32 SuperMini Development Board ESP32 Development Board WiFi Bluetooth.
  RFID RC522 SIP - 8 pins: A SIP stand-in part for RFID RC522 . With 8 pins on a 300 mil single inline package (SIP) footprint.
