# Fritzing sketch NFC_reader_switch_power (saved by Fritzing 1.0.1rc)
# 18650 Li-ion Battery: CC-BY Dr Kristofer Chan, King's College London/Remote-research.org
breadboards: 1

parts:
  BAT1 = 18650 Li-ion Battery [package=battery-18650]
  Sensor1 = TTP223B Capacitive Touch Sensor Module
  A1 = Esp32-c3 super mini
  Q1 = Basic FET N-Channel [package="TO220 [THT]"]

nets:
  N1: BAT1.-, Sensor1.GND, Q1.source
  N2: BAT1.+, Sensor1.VCC, A1.Pin_16
  N3: Sensor1.SIG, Q1.gate
  N4: A1.Pin_15, Q1.drain

notes:
  jump B soudé
  IRFZ34N
  zf240523.1356
  NFC_reader_switch_power zf240523.1359

custom parts:
  18650 Li-ion Battery: 18650 li-ion Battery Standard 18650 battery with interactive connectors Creative Common Attribution 4.0 International (CC-BY 4.0) license. Any use of this part requires attribution of Dr Kristofer Chan, Department of Geography, King's College London. Contact kristofer.chan [at] kcl.ac.uk OR kris [at] remote-research.org for further information.
  TTP223B Capacitive Touch Sensor Module: The TTP223B capacitive touch sensor module uses the TTP223B IC. The appropriate voltage is approximately 2 to 5.5 volts.
  Esp32-c3 super mini: ESP32-C3 Development Board ESP32 SuperMini Development Board ESP32 Development Board WiFi Bluetooth.
